# Fritzing sketch v20 (saved by Fritzing 0.9.3b)
perfboards: 1

parts:
  LED1 = smd LED [color="Red (633nm)" package="1206 [SMD]"]  # not connected
  LED2 = smd LED [color="Blue (430nm)" package="1206 [SMD]"]  # not connected
  DHT1 = DHT11 Humitidy and Temperature Sensor
  U1 = NodeMCU V1.0
  R1 = Resistor [tolerance=±5% resistance=220 package="2512 [SMD]"]  # not connected
  R2 = Resistor [tolerance=±5% resistance=220 package="2512 [SMD]"]  # not connected
  PIR1 = PIR sensor
  U2 = GAS_SENSOR [package=mq-3]

nets:
  VDD: DHT1.VDD, U1.3V3
  N1: DHT1.DATA, U1.D1
  N2: U1.D5, PIR1.SIG
  N3: U1.A0, U2.H2

custom parts:
  DHT11 Humitidy and Temperature Sensor: DHT11 Humidity and Temperature Sensor
  NodeMCU V1.0: ESP8266 based NodeMCU
